# Fritzing sketch Smart_Kos_Schematic (saved by Fritzing 0.9.2b)

parts:
  M1 = DOIT Esp32 DevKit v1 (30 pins long, 11 pins width) [part_number=ESP32S-PIN30]
  Part1 = Jtron 1 Channel Optoisolated Relay Module [package=relay]
  o1 = Module display OLED I2C 128x64 SSD1306 [package=THT]
  J1 = Piezo Speaker
  DHT11_1 = DHT11 module
  Part2 = SRF05 Ultrasonic Rangefinder
  F1 = Fan - Ventilador [package=THT]
  VCC1 = Battery block 9V
  JP1 = Header 6 [package=molex-1x6_lock]
  JP2 = Header 6 [package=molex-1x6_lock]
  JP3 = Header 1 [package=pad-1.5x4.5]
  JP4 = Header 8 [package=1x08_smd_alt]

nets:
  N1: M1.3V3, JP4.1
  N2: M1.GND, JP4.2
  N3: M1.D2, JP4.3
  N4: M1.D4, JP4.4
  N5: M1.D5, JP4.5
  N6: M1.D21, JP4.6
  N7: M1.D22, JP4.7
  N8: M1.D23, JP4.8
  N9: Part1.MAIN, VCC1.+
  N10: Part1.IN1, JP1.3
  N11: Part1.GND, JP1.2
  GND: o1.GND, Part2.GND
  N12: o1.SCL, JP2.6
  N13: o1.SDA, JP2.5
  N14: J1.pin2, JP3.1
  N15: DHT11_1.VCC, JP1.1
  N16: DHT11_1.DATA, JP1.4
  N17: Part2.Trig, JP2.4
  N18: Part2.Echo, JP2.3
  N19: F1.GND, VCC1.-

notes:
  Pin Dht 5
  Pin Relay 23
  Pin scl 22
  Pin sda 21
  Pin Buzzer 18
  Pin Echo 4
  Pin Trig 2

custom parts:
  DOIT Esp32 DevKit v1 (30 pins long, 11 pins width): The DOIT Esp32 DevKit v1 is one of the development board created by DOIT to evaluate the ESP-WROOM-32 module. It is based on the ESP32 microcontroller that boasts Wifi, Bluetooth, Ethernet and Low Power support all in a single chip. (vanepp) made breadboard work, adjusted pin numbering and labels and reduced size of schematic and cleaned up pcb. This chip is 30pins long (2 x15) and 11 pins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
  Module display OLED I2C 128x64 SSD1306: Ecran OLED I2C SSD163 de 128x64 avec connexion I2C
  DHT11 module: https://cdn-learn.adafruit.com/downloads/pdf/dht.pdf DHT11 black pcb module reference by:https://github.com/adafruit/Fritzing-Library/blob/master/parts/DHT11%20Humitidy%20and%20Temperature%20Sensor.fzpz
  Fan - Ventilador: Ventilador de 2 pines, se encuentra comunmente en computadoras de escritorio
